# Fritzing sketch ESP8266_oled_AP_ssd1306 (saved by Fritzing 0.9.3b)

parts:
  I2C_SSD1 = OLED 0.96" 128x64 I2C SSD1306
  U2 = NodeMCU V1.0
  R1 = Resistor [tolerance=±5% resistance=470k part_number=470kΩ package=THT]
  R2 = Resistor [tolerance=±5% resistance=470k package=THT]
  BAT1 = Battery Holders [package=lipo-1100mAh]

nets:
  VCC: I2C_SSD1.VCC, U2.3V3
  GND: I2C_SSD1.GND, U2.GND
  N1: I2C_SSD1.SCL, U2.D4
  N2: I2C_SSD1.SCA, U2.D2
  N3: U2.A0, R1.Pin_1
  N4: R1.Pin_0, BAT1.+
  N5: R2.Pin_0, BAT1.-

notes:
  Pause
  470kΩ

custom parts:
  NodeMCU V1.0: ESP8266 based NodeMCU V1.0
